# Fritzing sketch Trocknung_ArduinoNano (saved by Fritzing 1.0.4)
stripboards: 1

parts:
  LCM1602_IIC1 = LCM1602 IIC [part_number="LCM1602 IIC" chip_label="LCM1602 IIC" package="DIP (Dual Inline) [THT]"]
  U2 = LCD-16X2 [package=lcd-16x2_noholes]
  F3 = Fan - 4 wire [package=THT]  # not connected
  WATER_PUMP1 = gear-motor
  Bauteil3 = Adafruit SHT4x [part_number="Adafruit #4885"]
  Mod1 = generic-ac-power-supply [package=THT]
  A1 = DFR0379
  Bauteil4 = Lilypad Battery Connect
  Bauteil5 = Arduino Nano (Rev3.0)
  KY-1 = Keyes Relay [package=THT]
  F5 = Fan - 4 wire [package=THT]
  F6 = Fan - 4 wire [package=THT]  # not connected
  F7 = Fan - 4 wire [package=THT]

nets (from the breadboard view):
  VSS: LCM1602_IIC1.VSS, U2.VSS
  VDD: LCM1602_IIC1.VDD, U2.VDD
  N1: LCM1602_IIC1.V0, U2.VO
  N2: LCM1602_IIC1.RS, U2.RS
  N3: LCM1602_IIC1.RW, U2.R_W
  N4: LCM1602_IIC1.E, U2.E
  N5: LCM1602_IIC1.D0, U2.DB0
  N6: LCM1602_IIC1.D1, U2.DB1
  N7: LCM1602_IIC1.D2, U2.DB2
  N8: LCM1602_IIC1.D3, U2.DB3
  N9: LCM1602_IIC1.D4, U2.DB4
  N10: LCM1602_IIC1.D5, U2.DB5
  N11: LCM1602_IIC1.D6, U2.DB6
  N12: LCM1602_IIC1.D7, U2.DB7
  N13: LCM1602_IIC1.A, U2.A
  N14: LCM1602_IIC1.K, U2.K
  GND: LCM1602_IIC1.GND, Bauteil3.GND, Mod1.pin3#3, A1.Pin_4, A1.Pin_5, A1.Pin_6, Bauteil5.GND, KY-1.ground, F5.GND, F7.GND
  VCC: LCM1602_IIC1.VCC, Bauteil3.VCC, A1.Pin_7, A1.Pin_8, Bauteil5.VIN, KY-1.power
  N15: LCM1602_IIC1.SDA, Bauteil3.SDA, Bauteil5.A4
  N16: LCM1602_IIC1.SCL, Bauteil3.SCL, Bauteil5.A5
  N17: WATER_PUMP1.pin_1, KY-1.NO
  N18: WATER_PUMP1.pin_2, Mod1.pin1, Bauteil4.-
  N19: Mod1.pin2, Bauteil4.+, KY-1.C
  N20: Mod1.pin3#2, A1.Pin_1, F5.Power, F7.Power
  N21: Bauteil5.D3, F7.PWM
  N22: Bauteil5.D5, F5.PWM
  N23: Bauteil5.A0, KY-1.signal

notes:
  12 Volt Netzteil
  5V Stepdown Converter
  Stabile Versorgung für das Arduion Nano
  230 Volt Kompressor 3Ampere
  NO - Relay 230V
  230 Volt Versorgung >>
  LCD Display I2C 5Volt 2x16
  Gruppe Top Lüfter
  Gruppe Bottom Lüfter

custom parts:
  LCM1602 IIC: I2C-Module to use a 1602 or 2004 LCD on with the wire.h libory Serial LCD Modul
  Fan - 4 wire: Fan, 4 wire with tach.
  Adafruit SHT4x: Sensirion Temperature/Humidity sensors are some of the finest & highest-accuracy devices you can get. And finally, we have some that have a true I2C interface for easy reading. The SHT40 and SHT45 sensors are the fourth generation (started at the SHT10 and worked its way up to the top!). The SHT40 has an excellent ±1.8% typical relative humidity accuracy from 25 to 75% and ±0.2 °C typical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
  generic-ac-power-supply: Generic ac power supply module. Use as is, or customize the svgs to fit your particular device (as they are all different.) Provides AC input and single DC output. PCB is generic and will need modifications if you intend to do a pcb mount.
  DFR0379: 20W Adjustable DC-DC Buck Converter with Digital Display.
  Keyes Relay: The Keyes 5V relay module is suitable for SCM development, home appliance control. It uses a 5V~12V TIL control signal which can control DC / AC signal.
